// Logisim project Ejercicio1solucion.circ as structural Verilog: 1 circuit, main circuit main
module main (
  input  A1,
  input  A0,
  input  B1,
  input  B0,
  output Z
);

  wire and_1_out, and_2_out, and_3_out, and_4_out, not_1_out, not_2_out, not_3_out, not_4_out;

  not not_1 (not_1_out, A1);
  not not_2 (not_2_out, A0);
  not not_3 (not_3_out, B1);
  not not_4 (not_4_out, B0);
  and and_1 (and_1_out, not_1_out, not_2_out, B1);
  and and_2 (and_2_out, not_1_out, not_2_out, B0);
  and and_3 (and_3_out, A1, not_3_out, not_4_out);
  and and_4 (and_4_out, A0, not_3_out, not_4_out);
  or or_1 (Z, and_1_out, and_2_out, and_3_out, and_4_out);
endmodule
